# Fritzing sketch avr_breakout (saved by Fritzing 0.9.2b)
breadboards: 1

parts:
  JP2 = AVR ISP 6 Pin [package=2x3_lock]
  IC1 = ATmega328 [package=tqfp]
  C1 = Ceramic Capacitor [capacitance=100nF package="100 mil [THT, multilayer]"]
  R1 = Resistor [tolerance=±5% resistance=10k package=THT]

nets (from the schematic view):
  N1: JP2.1, IC1.PB4(MISO)
  5V: JP2.2, IC1.VCC, IC1.AVCC, IC1.AREF, R1.Pin_0
  N2: JP2.3, IC1.PB5(SCK)
  N3: JP2.4, IC1.PB3(MOSI_OC2)
  N4: JP2.5, IC1.PC6(_RESET), C1.1, R1.Pin_1
  GND: JP2.6, IC1.GND, IC1.AGND, C1.0

notes:
  This schematic compatible for:
  AVR Adaptor (www.sparkfun.com/products/8508)
